// Logisim project ALU CPU.circ as structural Verilog: 1 circuit, main circuit main
// Salida
module main (
  input  [31:0] Entrada_A,
  input  [31:0] in_2,
  input  [31:0] Entrada_B,
  input  [3:0] \Operación 
);

  Adder #(.width(32)) adder_1 ();  // open: a, b, out, cin, cout
  Multiplier #(.width(32)) multiplier_1 ();  // open: a, b, out, cin, cout
  Comparator #(.width(32)) comparator_1 ();  // open: a, b, gt, eq, lt
  Subtractor #(.width(32)) subtractor_1 ();  // open: a, b, out, bin, bout
  Divider #(.width(32)) divider_1 ();  // open: a, b, out, upper, rem
  Multiplexer #(.select(4), .width(32), .enable("false")) multiplexer_1 (.out(in_2));  // open: in0, in1, in2, in3, in4, in5, in6, in7, in8, in9, in10, in11, in12, in13, in14, in15, sel

  // Notes on the sheet:
  //   Multiplicación Sin Signo
  //   Suma
  //   Resta
  //   División sin signo
  //   Arithmetic Logic Unit
endmodule
