// Logisim project Branch Control.circ as structural Verilog: 2 circuits, main circuit Branch Control
module Branch_Control (
  input  N,
  input  [31:0] Constant_extended,
  input  [25:0] Destiny,
  input  [31:0] Register,
  input  Z,
  input  j,
  input  [31:0] PC,
  input  [2:0] Branch_Code,
  output [31:0] PC_prime
);

  wire [1:0] J_Sel;
  wire [31:0] Branch, Next_ins, shifter_1_out;

  Shifter #(.width(32)) shifter_1 (.in(Constant_extended), .\dist (5'b00010), .out(shifter_1_out));
  Adder #(.width(32)) adder_1 (.a(PC), .b(32'h4), .out(Next_ins));  // open: cin, cout
  Adder #(.width(32)) adder_2 (.a(shifter_1_out), .b(Next_ins), .out(Branch));  // open: cin, cout
  JUMP_B jump_b_1 (
    .jump(j), .B2(Branch_Code[2]), .B1(Branch_Code[1]), .B0(Branch_Code[0]), .Z(Z), .N(N), .out_7(J_Sel));
  Multiplexer #(.select(2), .width(32), .enable("false")) multiplexer_1 (
    .in0(Next_ins), .in1(Branch), .in2(Register), .in3({PC[31:28], Destiny, 2'b00}), .out(PC_prime),
    .sel(J_Sel));

  // Other names for the same wires on the sheet: B0 = Branch_Code[0]; B1 = Branch_Code[1]; B2 = Branch_Code[2];
  //   jmp = j; Jr[31:0] = Register; Jump[31:2] = {PC[31:28], Destiny}; Extend[3:0] = PC[31:28]

  // Notes on the sheet:
  //   Z: pull=down
  //   j: pull=down
  //   Branch_Code: pull=down
  //   N: pull=down
endmodule

module JUMP_B (
  input  jump,
  input  B2,
  input  B1,
  input  B0,
  input  Z,
  input  N,
  output [1:0] out_7
);

  wire and_2_out, and_3_out, and_4_out, and_5_out, and_6_out, and_7_out, not_1_out, not_2_out, not_3_out,
       not_4_out, not_5_out, not_6_out, not_7_out, not_8_out, not_9_out, not_10_out, not_11_out;

  and and_1 (out_7[1], jump, B2, B1);
  not not_1 (not_1_out, B2);
  not not_2 (not_2_out, B0);
  not not_3 (not_3_out, Z);
  not not_4 (not_4_out, B2);
  not not_5 (not_5_out, Z);
  not not_6 (not_6_out, B0);
  not not_7 (not_7_out, Z);
  not not_8 (not_8_out, N);
  not not_9 (not_9_out, B1);
  not not_10 (not_10_out, Z);
  not not_11 (not_11_out, B0);
  and and_2 (and_2_out, jump, not_1_out, B0, Z);
  and and_3 (and_3_out, jump, B1, not_2_out, not_3_out);
  and and_4 (and_4_out, jump, not_4_out, B1, not_5_out, N);
  and and_5 (and_5_out, jump, B2, not_6_out, not_7_out, not_8_out);
  and and_6 (and_6_out, jump, B2, not_9_out, B0, not_10_out, N);
  and and_7 (and_7_out, jump, B2, B1, not_11_out);
  or or_1 (out_7[0], and_2_out, and_3_out, and_4_out, and_5_out, and_6_out, and_7_out);
endmodule
