// Logisim project Control Unit.circ as structural Verilog: 5 circuits, main circuit Control Unit
module Control_Unit (
  input  in_1,
  input  in_2,
  input  [5:0] in_3,
  input  [5:0] in_4,
  input  [3:0] in_5,
  input  [3:0] in_6,
  output IorD,
  output [3:0] out_8,
  output END,
  output [1:0] RegDst,
  output [2:0] Branch_Control,
  output [2:0] ALU_SrcB,
  output [2:0] MemtoReg,
  output Dir_A,
  output Dir_B,
  output Inst_Write,
  output CS,
  output HI_LO_Write,
  output Load_A_B,
  output Load_ALU_HI,
  output RegWrite,
  output out_22,
  output DataWrite,
  output MemWrite,
  output tty_EN,
  output kbd_EN
);

  wire ALU_SrcB_0_00, ALU_SrcB_0_01, ALU_SrcB_0_02, ALU_SrcB_0_03, ALU_SrcB_2_00, ALU_SrcB_2_02, CS1, CS8,
       CS_02, CS_04, CS_05, CS_06, CS_07, d_ff_1_q, d_ff_2_q, d_ff_3_q, d_ff_16_q, d_ff_17_q, d_ff_18_q,
       d_ff_22_q, d_ff_23_q, d_ff_26_q, d_ff_29_q, demultiplexer_2_out0, demultiplexer_2_out3,
       demultiplexer_2_out4, demultiplexer_5_out0, demultiplexer_8_out1, demultiplexer_9_out1, Dir_A_00,
       Dir_A_01, IDLE_q, Load_A_B_00, Load_A_B_01, Load_A_B_02, Load_A_B_03, Load_A_B_04, Load_A_B_05,
       Load_A_B_06, Load_A_B_09, Load_A_B_10, Load_ALU_HI_00, Load_ALU_HI_02, MemtoReg0_00, MemtoReg0_01,
       MemtoReg0_02, MemtoReg0_03, MemtoReg1_02, MemtoReg2_01, nor_1_out, or_1_out, or_6_out, or_14_out,
       or_15_out, or_18_out, or_19_out, or_23_out, Push_pop, RegDst1_00, RegDst1_01, RegDst_0_00,
       RegWrite_01, RT__WT_RAM_Sel, wait_Ram;
  wire [1:0] Math_Op, Special_Op;
  wire [2:0] Op_sel;
  wire [3:0] counter_1_q, RT__WT;

  or or_1 (or_1_out, out_22, IDLE_q);
  D_Flip_Flop IDLE (.clk(in_2), .D(1'b0), .Q(IDLE_q), .preset(in_1));  // open: Qn, en, reset
  Multiplexer #(.width(4), .enable("false")) multiplexer_1 (.in0(in_5), .in1(in_6), .out(RT__WT), .sel(RT__WT_RAM_Sel));
  or or_2 (Dir_A, Dir_A_00, Dir_A_01);
  or or_3 (Load_ALU_HI, Load_ALU_HI_00, ALU_SrcB_0_00, Load_ALU_HI_02, ALU_SrcB_0_01, ALU_SrcB_0_02, ALU_SrcB_0_03, ALU_SrcB_2_02, ALU_SrcB_2_00);
  or or_4 (RegDst[1], RegDst1_00, RegDst1_01);
  or or_5 (RegWrite, MemtoReg0_00, RegWrite_01, RegDst_0_00, MemtoReg1_02, MemtoReg2_01, MemtoReg0_03, RegDst1_01, RegDst1_00, MemtoReg0_02, MemtoReg0_01);
  or or_6 (or_6_out, CS1, or_1_out);
  D_Flip_Flop d_ff_1 (.clk(in_2), .D(CS), .Q(d_ff_1_q), .reset(in_1));  // open: Qn, preset, en
  D_Flip_Flop d_ff_2 (.clk(in_2), .D(or_6_out), .Q(d_ff_2_q), .reset(in_1));  // open: Qn, preset, en
  Demultiplexer #(.enable("false")) demultiplexer_1 (.out0(CS1), .out1(Inst_Write), .in(d_ff_2_q), .sel(wait_Ram));
  // Probe on out_8
  ALU_Decoder alu_decoder_1 (.in_1(in_3), .in_2(in_4), .out_3(out_8));
  Branch_Control_Decoder branch_control_decoder_1 (.in_1(in_3), .in_2(in_4), .Branch_Control(Branch_Control));
  // Probe on Op_sel
  CU_Op_Decoder cu_op_decoder_1 (
    .in_1(in_3), .Op_CU(Op_sel), .in_2(in_4), .out_4(Push_pop), .out_5(Special_Op), .Math_OP(Math_Op));
  Counter #(.width(4), .max('hf)) counter_1 (
    .load(CS), .D(RT__WT), .count(d_ff_1_q), .Q(counter_1_q), .clk(in_2));  // open: carry, clr
  D_Flip_Flop d_ff_3 (.clk(in_2), .D(Inst_Write), .Q(d_ff_3_q), .reset(in_1));  // open: Qn, preset, en
  // Probe on Branch_Control
  nor nor_1 (nor_1_out, counter_1_q[0], counter_1_q[1], counter_1_q[2], counter_1_q[3]);
  or or_7 (ALU_SrcB[2], ALU_SrcB_2_00, ALU_SrcB_0_01, ALU_SrcB_2_02);
  or or_8 (MemtoReg[1], MemtoReg0_00, MemtoReg1_02);
  or or_9 (MemtoReg[2], MemtoReg2_01, MemtoReg0_01);
  Demultiplexer #(.select(3), .enable("false")) demultiplexer_2 (
    .out0(demultiplexer_2_out0), .out1(Load_A_B_03), .out2(Load_A_B_04), .out3(demultiplexer_2_out3),
    .out4(demultiplexer_2_out4), .out5(Load_A_B_09), .out6(Load_A_B_10), .out7(Load_A_B_06), .in(d_ff_3_q),
    .sel(Op_sel));
  and and_1 (wait_Ram, nor_1_out, d_ff_1_q);
  or or_10 (Load_A_B, Load_A_B_05, Load_A_B_00, Load_A_B_04, Load_A_B_01, Load_A_B_03, Load_A_B_02, Load_A_B_06, Load_A_B_10, Load_A_B_09, Dir_B, Dir_A_01, Dir_A_00);
  Demultiplexer #(.select(2), .enable("false")) demultiplexer_3 (
    .out0(Load_A_B_02), .out1(Load_A_B_01), .out2(Load_A_B_00), .in(demultiplexer_2_out0), .sel(Math_Op));  // open: out3
  Demultiplexer #(.enable("false")) demultiplexer_4 (
    .out0(Dir_A_00), .out1(Dir_A_01), .in(demultiplexer_2_out4), .sel(Push_pop));
  Demultiplexer #(.select(2), .enable("false")) demultiplexer_5 (
    .out0(demultiplexer_5_out0), .out1(MemtoReg2_01), .out2(Load_A_B_05), .out3(MemtoReg0_01),
    .in(demultiplexer_2_out3), .sel(Special_Op));
  D_Flip_Flop d_ff_4 (.clk(in_2), .D(Dir_A_01), .Q(ALU_SrcB_0_01), .reset(in_1));  // open: Qn, preset, en
  D_Flip_Flop d_ff_5 (.clk(in_2), .D(Load_A_B_09), .Q(ALU_SrcB_0_02), .reset(in_1));  // open: Qn, preset, en
  D_Flip_Flop d_ff_6 (.clk(in_2), .D(Load_A_B_10), .Q(ALU_SrcB_0_03), .reset(in_1));  // open: Qn, preset, en
  or or_11 (CS, Inst_Write, CS1, CS_02, CS_04, CS_05, CS_06, CS8, 1'b0, CS_07);
  or or_12 (RegDst[0], MemtoReg0_00, MemtoReg0_01, RegDst_0_00, MemtoReg1_02, MemtoReg2_01, MemtoReg0_02);
  D_Flip_Flop d_ff_7 (.clk(in_2), .D(Load_A_B_00), .Q(ALU_SrcB_0_00), .reset(in_1));  // open: Qn, preset, en
  D_Flip_Flop d_ff_8 (.clk(in_2), .D(Load_A_B_03), .Q(MemtoReg0_00), .reset(in_1));  // open: Qn, preset, en
  D_Flip_Flop d_ff_9 (.clk(in_2), .D(Load_A_B_04), .Q(MemtoReg1_02), .reset(in_1));  // open: Qn, preset, en
  D_Flip_Flop d_ff_10 (.clk(in_2), .D(Dir_A_00), .Q(ALU_SrcB_2_00), .reset(in_1));  // open: Qn, preset, en
  D_Flip_Flop d_ff_11 (.clk(in_2), .D(Load_A_B_02), .Q(Load_ALU_HI_00), .reset(in_1));  // open: Qn, preset, en
  D_Flip_Flop d_ff_12 (.clk(in_2), .D(Load_A_B_01), .Q(Load_ALU_HI_02), .reset(in_1));  // open: Qn, preset, en
  D_Flip_Flop d_ff_13 (.clk(in_2), .D(Load_A_B_05), .Q(tty_EN), .reset(in_1));  // open: Qn, preset, en
  or or_13 (ALU_SrcB[0], ALU_SrcB_0_00, ALU_SrcB_0_01, ALU_SrcB_0_02, ALU_SrcB_0_03);
  D_Flip_Flop d_ff_14 (.clk(in_2), .D(Load_ALU_HI_02), .Q(HI_LO_Write), .reset(in_1));  // open: Qn, preset, en
  D_Flip_Flop d_ff_15 (
    .clk(in_2), .D(demultiplexer_5_out0), .Q(END), .en(demultiplexer_5_out0), .reset(in_1));  // open: Qn, preset
  D_Flip_Flop d_ff_16 (.clk(in_2), .D(ALU_SrcB_0_01), .Q(d_ff_16_q), .reset(in_1));  // open: Qn, preset, en
  D_Flip_Flop d_ff_17 (.clk(in_2), .D(ALU_SrcB_0_02), .Q(d_ff_17_q), .reset(in_1));  // open: Qn, preset, en
  D_Flip_Flop d_ff_18 (.clk(in_2), .D(ALU_SrcB_0_03), .Q(d_ff_18_q), .reset(in_1));  // open: Qn, preset, en
  D_Flip_Flop d_ff_19 (.clk(in_2), .D(Load_ALU_HI_00), .Q(RegDst_0_00), .reset(in_1));  // open: Qn, preset, en
  D_Flip_Flop d_ff_20 (.clk(in_2), .D(ALU_SrcB_0_00), .Q(RegWrite_01), .reset(in_1));  // open: Qn, preset, en
  D_Flip_Flop d_ff_21 (.clk(in_2), .D(ALU_SrcB_2_00), .Q(RegDst1_00), .reset(in_1));  // open: Qn, preset, en
  or or_14 (or_14_out, CS_05, d_ff_16_q);
  or or_15 (or_15_out, CS_06, d_ff_17_q);
  or or_16 (MemtoReg[0], MemtoReg0_02, MemtoReg0_00, MemtoReg0_01, MemtoReg0_03);
  D_Flip_Flop d_ff_22 (.clk(in_2), .D(or_14_out), .Q(d_ff_22_q), .reset(in_1));  // open: Qn, preset, en
  Demultiplexer #(.enable("false")) demultiplexer_6 (.out0(CS_05), .out1(CS_04), .in(d_ff_22_q), .sel(wait_Ram));
  Demultiplexer #(.enable("false")) demultiplexer_7 (.out0(CS_06), .out1(CS_07), .in(d_ff_23_q), .sel(wait_Ram));
  D_Flip_Flop d_ff_23 (.clk(in_2), .D(or_15_out), .Q(d_ff_23_q), .reset(in_1));  // open: Qn, preset, en
  or or_17 (DataWrite, CS_07, CS_04);
  D_Flip_Flop d_ff_24 (.clk(in_2), .D(MemtoReg0_01), .Q(kbd_EN), .reset(in_1));  // open: Qn, preset, en
  D_Flip_Flop d_ff_25 (.clk(in_2), .D(RegDst1_00), .Q(Dir_B), .reset(in_1));  // open: Qn, preset, en
  Demultiplexer #(.enable("false")) demultiplexer_8 (
    .out0(CS8), .out1(demultiplexer_8_out1), .in(d_ff_26_q), .sel(wait_Ram));
  D_Flip_Flop d_ff_26 (.clk(in_2), .D(or_18_out), .Q(d_ff_26_q), .reset(in_1));  // open: Qn, preset, en
  or or_18 (or_18_out, CS8, d_ff_18_q);
  D_Flip_Flop d_ff_27 (.clk(in_2), .D(CS_04), .Q(MemtoReg0_02), .reset(in_1));  // open: Qn, preset, en
  or or_19 (or_19_out, CS_02, Dir_B);
  D_Flip_Flop d_ff_28 (.clk(in_2), .D(CS_07), .Q(MemtoReg0_03), .reset(in_1));  // open: Qn, preset, en
  Demultiplexer #(.enable("false")) demultiplexer_9 (
    .out0(CS_02), .out1(demultiplexer_9_out1), .in(d_ff_29_q), .sel(wait_Ram));
  D_Flip_Flop d_ff_29 (.clk(in_2), .D(or_19_out), .Q(d_ff_29_q), .reset(in_1));  // open: Qn, preset, en
  D_Flip_Flop d_ff_30 (.clk(in_2), .D(MemtoReg0_02), .Q(ALU_SrcB_2_02), .reset(in_1));  // open: Qn, preset, en
  D_Flip_Flop d_ff_31 (.clk(in_2), .D(ALU_SrcB_2_02), .Q(RegDst1_01), .reset(in_1));  // open: Qn, preset, en
  or or_20 (RT__WT_RAM_Sel, CS_02, CS8);
  or or_21 (IorD, CS_05, CS_06, CS_02, CS8, CS_07, CS_04);
  or or_22 (MemWrite, 1'b0, CS8, CS_02);
  or or_23 (or_23_out, RegDst_0_00, HI_LO_Write, RegWrite_01, MemtoReg0_00, MemtoReg1_02, MemtoReg2_01, tty_EN, kbd_EN, demultiplexer_9_out1, RegDst1_01, MemtoReg0_03, demultiplexer_8_out1, Load_A_B_06);
  D_Flip_Flop u_END (.clk(in_2), .D(or_23_out), .Q(out_22), .reset(in_1));  // open: Qn, preset, en

  assign ALU_SrcB[1] = 1'b0;

  // Other names for the same wires on the sheet: ALU_Op[3:0] = out_8; ALU_SrcB_0 = ALU_SrcB[0];
  //   ALU_SrcB_2 = ALU_SrcB[2]; Clk = in_2; CS0 = Inst_Write; Func_Code[5:0] = in_4; IorD_01 = CS_06;
  //   DataWrite_00 = CS_07; IorD_03 = CS_07; IorD_04 = CS_05; DataWrite_01 = CS_04; IorD_05 = CS_04;
  //   Load_A_B_07 = Dir_A_00; Load_A_B_08 = Dir_A_01; Load_A_B_11 = Dir_B; Load_ALU_HI_01 = ALU_SrcB_0_00;
  //   Load_ALU_HI_03 = ALU_SrcB_2_00; ALU_SrcB_2_01 = ALU_SrcB_0_01; Load_ALU_HI_04 = ALU_SrcB_0_01;
  //   Load_ALU_HI_05 = ALU_SrcB_2_02; Load_ALU_HI_06 = ALU_SrcB_0_02; Load_ALU_HI_07 = ALU_SrcB_0_03;
  //   Op_Code[5:0] = in_3; PC = out_22; RegDst_0 = RegDst[0]; RegDst_1 = RegDst[1]; RegWrite_00 = RegDst_0_00;
  //   MemtoReg1_01 = MemtoReg0_00; RegDst_0_02 = MemtoReg0_00; RegWrite_02 = MemtoReg0_00; RegDst_0_03 = MemtoReg1_02;
  //   RegWrite_03 = MemtoReg1_02; RegDst_0_01 = MemtoReg2_01; RegWrite_04 = MemtoReg2_01; MemtoReg2_00 = MemtoReg0_01;
  //   RegDst_0_04 = MemtoReg0_01; RegWrite_05 = MemtoReg0_01; RegWrite_06 = RegDst1_00; RegWrite_07 = MemtoReg0_03;
  //   RegDst_0_05 = MemtoReg0_02; RegWrite_08 = MemtoReg0_02; RegWrite_09 = RegDst1_01; Reset = in_1; RT[3:0] = in_5;
  //   IorD_00 = CS_02; MemWrite_01 = CS_02; RT__WT_RAM_Sel_00 = CS_02; IorD_02 = CS8; MemWrite_02 = CS8;
  //   RT__WT_RAM_Sel_01 = CS8; WT[3:0] = in_6

  // Notes on the sheet:
  //   Input Data
  //   push
  //   N * / ALU
  //   lo
  //   Control Unit
  //   hi
  //   pop
  //   * / Alu
  //   inmediatos
  //   tty
  //   kbd
  //   rnd
  //   sw
  //   lw
  //   Output Data
endmodule

module ALU_Decoder (
  input  [5:0] in_1,
  input  [5:0] in_2,
  output [3:0] out_3
);

  wire A_value, add, add_ALU, addi, \and , and_ALU, andi, beq, bgtz, blez, bltz, bne, div, divu, halt, j, jr,
       kbd, lw, Math_op_out, mfhi, mflo, mflo_hi, mult, mulu, nop, \nor , \or , or_ALU, ori, pop, pop_v,
       push, push_pop, push_v, rnd, slt, slt_ALU, slti, sltiu, sltu, sltu_ALU, Special_out, sub, sub_ALU, sw,
       tty, \xor , xor_ALU, xori;

  and Math_op (Math_op_out, ~in_1[0], ~in_1[1], ~in_1[2], ~in_1[3], ~in_1[4], ~in_1[5]);  // AND_Gate
  and pop_push (push_pop, ~in_1[0], ~in_1[1], ~in_1[2], in_1[3], in_1[4], in_1[5]);  // AND_Gate
  and Special (Special_out, in_1[0], in_1[1], in_1[2], in_1[3], in_1[4], in_1[5]);
  and u_add (add, ~in_2[0], ~in_2[1], ~in_2[2], ~in_2[3], ~in_2[4], in_2[5]);  // AND_Gate
  and u_div (div, ~in_2[0], in_2[1], ~in_2[2], in_2[3], in_2[4], ~in_2[5]);  // AND_Gate
  and u_nor (\nor , in_2[0], in_2[1], in_2[2], ~in_2[3], ~in_2[4], in_2[5]);  // AND_Gate
  and u_mfhi (mfhi, ~in_2[0], ~in_2[1], ~in_2[2], ~in_2[3], in_2[4], ~in_2[5]);  // AND_Gate
  and u_halt (halt, in_2[0], in_2[1], in_2[2], in_2[3], in_2[4], in_2[5]);
  and u_Sub (sub, ~in_2[0], in_2[1], ~in_2[2], ~in_2[3], ~in_2[4], in_2[5]);  // AND_Gate
  and u_divu (divu, in_2[0], in_2[1], ~in_2[2], in_2[3], in_2[4], ~in_2[5]);  // AND_Gate
  and u_xor (\xor , ~in_2[0], ~in_2[1], ~in_2[2], in_2[3], ~in_2[4], in_2[5]);  // AND_Gate
  and u_mflo (mflo, ~in_2[0], in_2[1], ~in_2[2], ~in_2[3], in_2[4], ~in_2[5]);  // AND_Gate
  and u_tty (tty, in_2[0], ~in_2[1], ~in_2[2], ~in_2[3], ~in_2[4], ~in_2[5]);  // AND_Gate
  and u_addi (addi, ~in_1[0], ~in_1[1], ~in_1[2], in_1[3], ~in_1[4], ~in_1[5]);  // AND_Gate
  and u_andi (andi, ~in_1[0], ~in_1[1], in_1[2], in_1[3], ~in_1[4], ~in_1[5]);  // AND_Gate
  and u_slti (slti, ~in_1[0], in_1[1], ~in_1[2], in_1[3], ~in_1[4], ~in_1[5]);  // AND_Gate
  and u_beq (beq, ~in_1[0], ~in_1[1], in_1[2], ~in_1[3], ~in_1[4], ~in_1[5]);  // AND_Gate
  and u_bne (bne, in_1[0], ~in_1[1], in_1[2], ~in_1[3], ~in_1[4], ~in_1[5]);  // AND_Gate
  and u_mult (mult, ~in_2[0], ~in_2[1], ~in_2[2], in_2[3], in_2[4], ~in_2[5]);  // AND_Gate
  and u_and (\and , ~in_2[0], ~in_2[1], in_2[2], ~in_2[3], ~in_2[4], in_2[5]);  // AND_Gate
  and u_slt (slt, ~in_2[0], in_2[1], ~in_2[2], in_2[3], ~in_2[4], in_2[5]);  // AND_Gate
  and u_nop (nop, ~in_2[0], ~in_2[1], ~in_2[2], ~in_2[3], ~in_2[4], ~in_2[5]);  // AND_Gate
  and u_rnd (rnd, ~in_2[0], in_2[1], ~in_2[2], ~in_2[3], ~in_2[4], ~in_2[5]);  // AND_Gate
  and u_blez (blez, ~in_1[0], in_1[1], in_1[2], ~in_1[3], ~in_1[4], ~in_1[5]);  // AND_Gate
  and u_bgtz (bgtz, in_1[0], in_1[1], in_1[2], ~in_1[3], ~in_1[4], ~in_1[5]);  // AND_Gate
  and u_bltz (bltz, in_1[0], ~in_1[1], ~in_1[2], ~in_1[3], ~in_1[4], ~in_1[5]);  // AND_Gate
  and u_lw (lw, in_1[0], in_1[1], ~in_1[2], ~in_1[3], ~in_1[4], in_1[5]);  // AND_Gate
  and u_sw (sw, in_1[0], in_1[1], ~in_1[2], in_1[3], ~in_1[4], in_1[5]);  // AND_Gate
  and u_sltiu (sltiu, in_1[0], in_1[1], ~in_1[2], in_1[3], ~in_1[4], ~in_1[5]);  // AND_Gate
  and u_ori (ori, in_1[0], ~in_1[1], in_1[2], in_1[3], ~in_1[4], ~in_1[5]);  // AND_Gate
  and u_xori (xori, ~in_1[0], in_1[1], in_1[2], in_1[3], ~in_1[4], ~in_1[5]);  // AND_Gate
  and u_mulu (mulu, in_2[0], ~in_2[1], ~in_2[2], in_2[3], in_2[4], ~in_2[5]);  // AND_Gate
  and u_or (\or , in_2[0], ~in_2[1], in_2[2], ~in_2[3], ~in_2[4], in_2[5]);  // AND_Gate
  and u_sltu (sltu, in_2[0], in_2[1], ~in_2[2], in_2[3], ~in_2[4], in_2[5]);  // AND_Gate
  and u_jr (jr, ~in_2[0], ~in_2[1], ~in_2[2], in_2[3], ~in_2[4], ~in_2[5]);  // AND_Gate
  and u_kbd (kbd, ~in_2[0], ~in_2[1], in_2[2], ~in_2[3], ~in_2[4], ~in_2[5]);  // AND_Gate
  or or_2 (and_ALU, \and , andi);
  or or_3 (or_ALU, \or , ori);
  or u_mflo_hi (mflo_hi, mflo, mfhi);
  Priority_Encoder #(.select(4)) priority_encoder_1 (
    .in0(mult), .in1(mulu), .in2(div), .in3(divu), .in4(and_ALU), .in5(sub_ALU), .in6(xor_ALU),
    .in7(add_ALU), .in8(or_ALU), .in9(sltu_ALU), .in10(\nor ), .in11(slt_ALU), .in12(mflo_hi),
    .in13(A_value), .out(out_3));  // open: in14, in15, gs, en_out, en_in
  and and_2 (push_v, push_pop, push);
  or or_4 (slt_ALU, slt, slti);
  or or_5 (sltu_ALU, sltu, sltiu);
  or or_6 (xor_ALU, \xor , xori);
  and u_j (j, ~in_1[0], in_1[1], ~in_1[2], ~in_1[3], ~in_1[4], ~in_1[5]);  // AND_Gate
  and u_push (push, in_2[0], ~in_2[1], ~in_2[2], ~in_2[3], ~in_2[4], ~in_2[5]);  // AND_Gate
  and u_pop (pop, ~in_2[0], ~in_2[1], ~in_2[2], ~in_2[3], ~in_2[4], ~in_2[5]);  // AND_Gate
  or or_7 (sub_ALU, beq, sub, bne, push_v);
  and and_3 (pop_v, pop, push_pop);
  or or_8 (A_value, blez, bltz, bgtz);
  or or_9 (add_ALU, lw, add, pop_v, addi, sw);

  // Other names for the same wires on the sheet: ALU_OP_Code[3:0] = out_3; Func_code[5:0] = in_2; Op_Code[5:0] = in_1

  // Notes on the sheet:
  //   Op-Code
  //   Tipo R
  //   Func-Code
  //   Tipo I
  //   Tipo J
endmodule

module Branch_Control_Decoder (
  input  [5:0] in_1,
  input  [5:0] in_2,
  output [2:0] Branch_Control
);

  wire beq, bgtz, blez, bltz, bne, j, jr, jr_out, Math, nop, nop_out, Sel;
  wire [2:0] Branch_Control_t;

  and u_nop (nop_out, ~in_2[0], ~in_2[1], ~in_2[2], ~in_2[3], ~in_2[4], ~in_2[5]);  // AND_Gate
  and and_1 (nop, nop_out, Math);
  and Math_op (Math, ~in_1[0], ~in_1[1], ~in_1[2], ~in_1[3], ~in_1[4], ~in_1[5]);  // AND_Gate
  Priority_Encoder priority_encoder_1 (
    .in0(nop), .in1(beq), .in2(bne), .in3(blez), .in4(bgtz), .in5(bltz), .in6(j), .in7(jr),
    .out(Branch_Control_t), .en_out(Sel));  // open: en_in, gs
  and u_jr (jr_out, ~in_2[0], ~in_2[1], ~in_2[2], in_2[3], ~in_2[4], ~in_2[5]);  // AND_Gate
  and and_2 (jr, jr_out, Math);
  and u_beq (beq, ~in_1[0], ~in_1[1], in_1[2], ~in_1[3], ~in_1[4], ~in_1[5]);  // AND_Gate
  and u_bne (bne, in_1[0], ~in_1[1], in_1[2], ~in_1[3], ~in_1[4], ~in_1[5]);  // AND_Gate
  and u_blez (blez, ~in_1[0], in_1[1], in_1[2], ~in_1[3], ~in_1[4], ~in_1[5]);  // AND_Gate
  and u_bgtz (bgtz, in_1[0], in_1[1], in_1[2], ~in_1[3], ~in_1[4], ~in_1[5]);  // AND_Gate
  and u_bltz (bltz, in_1[0], ~in_1[1], ~in_1[2], ~in_1[3], ~in_1[4], ~in_1[5]);  // AND_Gate
  and u_j (j, ~in_1[0], in_1[1], ~in_1[2], ~in_1[3], ~in_1[4], ~in_1[5]);  // AND_Gate
  Multiplexer #(.width(3), .enable("false")) multiplexer_1 (
    .in0(Branch_Control_t), .in1(3'b000), .out(Branch_Control), .sel(Sel));

  // Other names for the same wires on the sheet: Func_code[5:0] = in_2; Op_Code[5:0] = in_1
endmodule

module CU_Op_Decoder (
  input  [5:0] in_1,
  input  [5:0] in_2,
  output [2:0] Op_CU,
  output out_4,
  output [1:0] out_5,
  output [1:0] Math_OP
);

  wire addi, andi, beq, bgtz, blez, bltz, bne, div, divu, halt, inm, j, jr, jr_out, jumps, kbd, lw, Math,
       mfhi, mfhi_out, mflo, mflo_out, mult, mulu, N, nop, nop_out, or_1_out, ori, priority_encoder_1_en_out,
       priority_encoder_2_en_out, push_pop, rnd, slti, sltiu, special, sw, tty, tunnel, xori;
  wire [1:0] priority_encoder_1_out, priority_encoder_2_out;

  and u_jr (jr_out, ~in_2[0], ~in_2[1], ~in_2[2], in_2[3], ~in_2[4], ~in_2[5]);  // AND_Gate
  and and_1 (jr, jr_out, Math);
  and u_beq (beq, ~in_1[0], ~in_1[1], in_1[2], ~in_1[3], ~in_1[4], ~in_1[5]);  // AND_Gate
  and u_bne (bne, in_1[0], ~in_1[1], in_1[2], ~in_1[3], ~in_1[4], ~in_1[5]);  // AND_Gate
  and u_Math_op (Math, ~in_1[0], ~in_1[1], ~in_1[2], ~in_1[3], ~in_1[4], ~in_1[5]);  // AND_Gate
  and pop_push (push_pop, ~in_1[0], ~in_1[1], ~in_1[2], in_1[3], in_1[4], in_1[5]);  // AND_Gate
  and u_Special (special, in_1[0], in_1[1], in_1[2], in_1[3], in_1[4], in_1[5]);
  and u_halt (halt, in_2[0], in_2[1], in_2[2], in_2[3], in_2[4], in_2[5]);
  and u_blez (blez, ~in_1[0], in_1[1], in_1[2], ~in_1[3], ~in_1[4], ~in_1[5]);  // AND_Gate
  and u_bgtz (bgtz, in_1[0], in_1[1], in_1[2], ~in_1[3], ~in_1[4], ~in_1[5]);  // AND_Gate
  and u_bltz (bltz, in_1[0], ~in_1[1], ~in_1[2], ~in_1[3], ~in_1[4], ~in_1[5]);  // AND_Gate
  and u_divu (divu, in_2[0], in_2[1], ~in_2[2], in_2[3], in_2[4], ~in_2[5]);  // AND_Gate
  and u_div (div, ~in_2[0], in_2[1], ~in_2[2], in_2[3], in_2[4], ~in_2[5]);  // AND_Gate
  and u_mfhi (mfhi_out, ~in_2[0], ~in_2[1], ~in_2[2], ~in_2[3], in_2[4], ~in_2[5]);  // AND_Gate
  or or_1 (or_1_out, mult, divu, mulu, div);
  and u_tty (tty, in_2[0], ~in_2[1], ~in_2[2], ~in_2[3], ~in_2[4], ~in_2[5]);  // AND_Gate
  and u_j (j, ~in_1[0], in_1[1], ~in_1[2], ~in_1[3], ~in_1[4], ~in_1[5]);  // AND_Gate
  or or_2 (jumps, beq, bne, blez, bgtz, bltz, nop, j, jr);
  and and_2 (mfhi, Math, mfhi_out);
  and and_3 (tunnel, or_1_out, Math);
  and u_N (N, ~tunnel, Math);  // AND_Gate
  and and_4 (nop, Math, nop_out);
  and u_nop (nop_out, ~in_2[0], ~in_2[1], ~in_2[2], ~in_2[3], ~in_2[4], ~in_2[5]);  // AND_Gate
  and u_mult (mult, ~in_2[0], ~in_2[1], ~in_2[2], in_2[3], in_2[4], ~in_2[5]);  // AND_Gate
  and u_mulu (mulu, in_2[0], ~in_2[1], ~in_2[2], in_2[3], in_2[4], ~in_2[5]);  // AND_Gate
  and u_mflo (mflo_out, ~in_2[0], in_2[1], ~in_2[2], ~in_2[3], in_2[4], ~in_2[5]);  // AND_Gate
  and pop (out_4, ~in_2[0], ~in_2[1], ~in_2[2], ~in_2[3], ~in_2[4], ~in_2[5]);  // AND_Gate
  and u_rnd (rnd, ~in_2[0], in_2[1], ~in_2[2], ~in_2[3], ~in_2[4], ~in_2[5]);  // AND_Gate
  and u_sltiu (sltiu, in_1[0], in_1[1], ~in_1[2], in_1[3], ~in_1[4], ~in_1[5]);  // AND_Gate
  and u_ori (ori, in_1[0], ~in_1[1], in_1[2], in_1[3], ~in_1[4], ~in_1[5]);  // AND_Gate
  and u_xori (xori, ~in_1[0], in_1[1], in_1[2], in_1[3], ~in_1[4], ~in_1[5]);  // AND_Gate
  and and_5 (mflo, Math, mflo_out);
  and u_lw (lw, in_1[0], in_1[1], ~in_1[2], ~in_1[3], ~in_1[4], in_1[5]);  // AND_Gate
  and u_sw (sw, in_1[0], in_1[1], ~in_1[2], in_1[3], ~in_1[4], in_1[5]);  // AND_Gate
  and u_kbd (kbd, ~in_2[0], ~in_2[1], in_2[2], ~in_2[3], ~in_2[4], ~in_2[5]);  // AND_Gate
  and u_addi (addi, ~in_1[0], ~in_1[1], ~in_1[2], in_1[3], ~in_1[4], ~in_1[5]);  // AND_Gate
  and u_andi (andi, ~in_1[0], ~in_1[1], in_1[2], in_1[3], ~in_1[4], ~in_1[5]);  // AND_Gate
  and u_slti (slti, ~in_1[0], in_1[1], ~in_1[2], in_1[3], ~in_1[4], ~in_1[5]);  // AND_Gate
  or or_3 (inm, sltiu, ori, xori, addi, andi, slti);
  Priority_Encoder #(.select(2)) priority_encoder_1 (
    .in0(halt), .in1(rnd), .in2(tty), .in3(kbd), .out(priority_encoder_1_out),
    .en_out(priority_encoder_1_en_out));  // open: gs, en_in
  Multiplexer #(.width(2), .enable("false")) multiplexer_1 (
    .in0(priority_encoder_1_out), .in1(2'b00), .out(out_5), .sel(priority_encoder_1_en_out));
  Priority_Encoder #(.select(2)) priority_encoder_2 (
    .in0(N), .in1(tunnel), .in2(inm), .out(priority_encoder_2_out), .en_out(priority_encoder_2_en_out));  // open: in3, gs, en_in
  Multiplexer #(.width(2), .enable("false")) multiplexer_2 (
    .in0(priority_encoder_2_out), .in1(2'b00), .out(Math_OP), .sel(priority_encoder_2_en_out));
  or or_4 (Op_CU[0], mfhi, special, lw, jumps);
  or or_5 (Op_CU[1], mflo, special, sw, jumps);
  or or_6 (Op_CU[2], lw, sw, push_pop, jumps);

  // Other names for the same wires on the sheet: Func_code[5:0] = in_2; Op_Code[5:0] = in_1; pop = out_4;
  //   Special_Op[1:0] = out_5
endmodule

module gbdfb (
  output CS
);

  wire ALU_SrcB_0, Clk, CS_t, d_ff_13_q, demultiplexer_1_out0, demultiplexer_1_out1, demultiplexer_2_out1,
       demultiplexer_3_out0, HI_LO_Write, IorD, Load_A_B, or_1_out, or_2_out, or_3_out, or_4_out, RegDst,
       Reset, undriven, wait_Ram;

  D_Flip_Flop d_ff_1 (.clk(Clk), .reset(Reset));  // open: D, Q, Qn, preset, en
  D_Flip_Flop d_ff_2 (.clk(Clk), .reset(Reset));  // open: D, Q, Qn, preset, en
  D_Flip_Flop d_ff_3 (.clk(Clk), .reset(Reset));  // open: D, Q, Qn, preset, en
  D_Flip_Flop d_ff_4 (.clk(Clk), .reset(Reset));  // open: D, Q, Qn, preset, en
  D_Flip_Flop d_ff_5 (.clk(Clk), .reset(Reset));  // open: D, Q, Qn, preset, en
  D_Flip_Flop d_ff_6 (.clk(Clk), .reset(Reset));  // open: D, Q, Qn, preset, en
  D_Flip_Flop d_ff_7 (.clk(Clk), .reset(Reset));  // open: D, Q, Qn, preset, en
  D_Flip_Flop d_ff_8 (.clk(Clk), .reset(Reset));  // open: D, Q, Qn, preset, en
  D_Flip_Flop d_ff_9 (.clk(Clk), .reset(Reset));  // open: D, Q, Qn, preset, en
  // D_Flip_Flop d_ff_10: pin names not known; wires that end beside it: ALU_SrcB_0, Clk, Reset, CS_t
  D_Flip_Flop d_ff_11 (.clk(Clk), .D(undriven), .Q(CS), .en(undriven), .reset(Reset));  // open: Qn, preset
  D_Flip_Flop d_ff_12 (.clk(Clk), .reset(Reset));  // open: D, Q, Qn, preset, en
  Demultiplexer #(.enable("false")) demultiplexer_1 (
    .out0(demultiplexer_1_out0), .out1(demultiplexer_1_out1), .in(d_ff_13_q), .sel(wait_Ram));
  D_Flip_Flop d_ff_13 (.clk(Clk), .D(or_1_out), .Q(d_ff_13_q), .reset(Reset));  // open: Qn, preset, en
  // OR_Gate or_1 has open pins: out=or_1_out
  D_Flip_Flop d_ff_14 (.clk(Clk), .reset(Reset));  // open: D, Q, Qn, preset, en
  D_Flip_Flop d_ff_15 (.clk(Clk), .reset(Reset));  // open: D, Q, Qn, preset, en
  D_Flip_Flop d_ff_16 (.clk(Clk), .reset(Reset));  // open: D, Q, Qn, preset, en
  D_Flip_Flop d_ff_17 (.clk(Clk), .reset(Reset));  // open: D, Q, Qn, preset, en
  // D_Flip_Flop d_ff_18: pin names not known; wires that end beside it: RegDst, Clk, Reset, IorD
  D_Flip_Flop d_ff_19 (.clk(Clk), .reset(Reset));  // open: D, Q, Qn, preset, en
  // OR_Gate or_2 has open pins: out=or_2_out
  D_Flip_Flop d_ff_20 (.clk(Clk), .reset(Reset));  // open: D, Q, Qn, preset, en
  D_Flip_Flop d_ff_21 (.clk(Clk), .reset(Reset));  // open: D, Q, Qn, preset, en
  Demultiplexer #(.enable("false")) demultiplexer_2 (.out0(CS_t), .out1(demultiplexer_2_out1));  // open: in, sel
  D_Flip_Flop d_ff_22 (.clk(Clk), .D(or_2_out), .reset(Reset));  // open: Q, Qn, preset, en
  // OR_Gate or_3 has open pins: out=or_3_out
  // OR_Gate or_4 has open pins: out=or_4_out
  Demultiplexer #(.enable("false")) demultiplexer_3 (.out0(demultiplexer_3_out0));  // open: out1, in, sel
  D_Flip_Flop d_ff_23 (.clk(Clk), .D(or_3_out), .reset(Reset));  // open: Q, Qn, preset, en
  D_Flip_Flop d_ff_24 (.clk(Clk), .D(or_4_out), .reset(Reset));  // open: Q, Qn, preset, en
  // Demultiplexer #(.enable("false")) demultiplexer_4: pin names not known; wires that end beside it: wait_Ram, CS_t
  D_Flip_Flop d_ff_25 (.clk(Clk), .reset(Reset));  // open: D, Q, Qn, preset, en
  D_Flip_Flop d_ff_26 (.clk(Clk), .reset(Reset));  // open: D, Q, Qn, preset, en
  D_Flip_Flop d_ff_27 (.clk(Clk), .D(Load_A_B), .Q(ALU_SrcB_0), .reset(Reset));  // open: Qn, preset, en
  D_Flip_Flop d_ff_28 (.clk(Clk), .reset(Reset));  // open: D, Q, Qn, preset, en
  D_Flip_Flop d_ff_29 (.clk(Clk), .D(Load_A_B), .Q(ALU_SrcB_0), .reset(Reset));  // open: Qn, preset, en
  D_Flip_Flop d_ff_30 (.clk(Clk), .D(Load_A_B), .Q(ALU_SrcB_0), .reset(Reset));  // open: Qn, preset, en
  D_Flip_Flop d_ff_31 (.clk(Clk), .D(ALU_SrcB_0), .Q(RegDst), .reset(Reset));  // open: Qn, preset, en
  D_Flip_Flop d_ff_32 (.clk(Clk), .D(ALU_SrcB_0), .Q(HI_LO_Write), .reset(Reset));  // open: Qn, preset, en
  D_Flip_Flop d_ff_33 (.clk(Clk), .D(ALU_SrcB_0), .Q(RegDst), .reset(Reset));  // open: Qn, preset, en

  // Other names for the same wires on the sheet: Load_ALU_HI = ALU_SrcB_0; RegWrite = RegDst

  // Notes on the sheet:
  //   pop
  //   push
  //   hi
  //   lo
  //   halt
  //   rnd
  //   tty
  //   kbd
  //   N * / ALU
  //   lw
  //   sw
  //   inmediatos
  //   * / Alu
endmodule
