// Logisim project DathaPath.circ as structural Verilog: 2 circuits, main circuit DataPath
module DataPath (
  input  [31:0] in_1,
  input  [31:0] in_2,
  input  [6:0] ASCII,
  input  [31:0] in_4,
  input  [31:0] in_5,
  input  [3:0] ALU_Op,
  input  [2:0] Branch_Code,
  input  [2:0] ALUSrcB,
  input  [2:0] MemtoReg,
  input  [1:0] RegDst,
  input  Dir_A,
  input  Dir_B,
  input  Kbd_available,
  input  DataWrite,
  input  Load_ALU_HI,
  input  Load_A_and_B,
  input  HI_LO_Write,
  input  RegWrite,
  input  jump,
  input  PCWrite,
  input  IorD,
  input  IRWrite,
  input  CLK,
  input  RST,
  output [31:0] out_25,
  output [31:0] out_26,
  output [31:0] out_27,
  output [31:0] out_28,
  output [15:0] Address,
  output [3:0] MASK,
  output [5:0] out_31,
  output [5:0] out_32,
  output [6:0] out_33
);

  wire NF, ZF;
  wire [4:0] Dir_Rd, Dir_Rs, Dir_Rt, multiplexer_4_out, multiplexer_5_out, multiplexer_6_out;
  wire [15:0] offset;
  wire [25:0] Dir_Salto;
  wire [31:0] A, ALU_Out, ASCII_t, B, B_out, Data_out, HI, HI_O, HI_Out, Instr_q,
       instruction_data_memory_1_out_7, LO, LO_O, multiplexer_1_out, multiplexer_2_out, multiplexer_3_out,
       multiplexer_7_out, offset_ext, PC, PC_prime, rnd, ZF_high, ZF_result_low;
  wire [31:7] A_out;

  Register #(.width(32)) u_PC (.D(PC_prime), .en(jump), .Q(PC), .clk(CLK), .clr(RST));
  assign ASCII_t = {{25{1'b0}}, ASCII};  // Bit_Extender bit_extender_1
  Multiplexer #(.width(32), .enable("false")) multiplexer_1 (
    .in0(PC), .in1(ALU_Out), .out(multiplexer_1_out), .sel(IorD));
  Instruction_Data_Memory instruction_data_memory_1 (
    .Address(multiplexer_1_out), .in_6(B), .out_7(instruction_data_memory_1_out_7), .in_1(in_1), .in_2(in_2),
    .in_3(in_4), .in_4(in_5), .out_8(out_25), .out_9(out_26), .out_10(out_27), .out_11(out_28),
    .Address_2(Address), .MASK(MASK));
  // Probe on instruction_data_memory_1_out_7
  // OR_Gate or_1 is placed but not wired
  Register #(.width(32)) Instr (
    .D(instruction_data_memory_1_out_7), .en(IRWrite), .Q(Instr_q), .clk(CLK));  // open: clr
  Register #(.width(32)) Data (
    .D(instruction_data_memory_1_out_7), .en(DataWrite), .Q(Data_out), .clk(CLK));  // open: clr
  Random #(.width(32)) random_1 (.clk(CLK), .out(rnd));  // open: next, clr
  Instruction_Decoder instruction_decoder_1 (
    .Instruction(Instr_q), .out_2(Dir_Salto), .out_5(Dir_Rd), .out_4(Dir_Rt), .out_3(Dir_Rs), .out_6(offset),
    .out_7(out_31), .out_8(out_32));
  assign offset_ext = {{16{offset[15]}}, offset};  // Bit_Extender bit_extender_2
  Multiplexer #(.width(32), .enable("false")) multiplexer_2 (
    .in0({32{1'b1}}), .in1(ASCII_t), .out(multiplexer_2_out), .sel(Kbd_available));
  Branch_Control branch_control_1 (
    .N(NF), .Z(ZF), .j(jump), .PC(PC), .Branch_Code(Branch_Code), .PC_prime(PC_prime),
    .Constant_extended(offset_ext), .Destiny(Dir_Salto), .Register(A));
  Multiplexer #(.select(3), .width(32), .enable("false")) multiplexer_3 (
    .in0(ALU_Out), .in1(Data_out), .in2(LO), .in3(HI), .in4(rnd), .in5(multiplexer_2_out),
    .out(multiplexer_3_out), .sel(MemtoReg));  // open: in6, in7
  Multiplexer #(.select(2), .width(5), .enable("false")) multiplexer_4 (
    .in0(Dir_Rt), .in1(Dir_Rd), .in2({5{1'b1}}), .out(multiplexer_4_out), .sel(RegDst));  // open: in3
  Multiplexer #(.width(5), .enable("false")) multiplexer_5 (
    .in0(Dir_Rs), .in1({5{1'b1}}), .out(multiplexer_5_out), .sel(Dir_A));
  Register_File_CPU_main main_1 (
    .\Dirección_de_destino (multiplexer_4_out), .R_W(RegWrite), .Datos_de_entrada(multiplexer_3_out),
    .Selector_Salida_A(multiplexer_5_out), .Selector_Salida_B(multiplexer_6_out), .Reset(RST), .Clock(CLK),
    .HI_in(HI_Out), .LO_in(ALU_Out), .R_W_HI_LO(HI_LO_Write), .Salida_A({A_out, out_33}), .Salida_B(B_out),
    .out_13(HI_O), .out_14(LO_O));
  Multiplexer #(.width(5), .enable("false")) multiplexer_6 (
    .in0(Dir_Rt), .in1(Dir_Rs), .out(multiplexer_6_out), .sel(Dir_B));
  Register #(.width(32)) u_A (.D({A_out, out_33}), .en(Load_A_and_B), .Q(A), .clk(CLK));  // open: clr
  Register #(.width(32)) u_B (.D(B_out), .en(Load_A_and_B), .Q(B), .clk(CLK));  // open: clr
  Register #(.width(32)) u_HI (.D(HI_O), .en(Load_A_and_B), .Q(HI), .clk(CLK));  // open: clr
  Register #(.width(32)) u_LO (.D(LO_O), .en(Load_A_and_B), .Q(LO), .clk(CLK));  // open: clr
  Multiplexer #(.select(3), .width(32), .enable("false")) multiplexer_7 (
    .in0(B), .in1(offset_ext), .in2(HI), .in3(LO), .in4(32'h4), .in5({32{1'b0}}), .out(multiplexer_7_out),
    .sel(ALUSrcB));  // open: in6, in7
  ALU u_ZF (
    .Input_0(A), .Input_1(multiplexer_7_out), .OpCode(ALU_Op), .Result_Low(ZF_result_low), .High(ZF_high),
    .ZF(ZF), .NF(NF));
  Register #(.width(32)) u_ALU_Out (.D(ZF_result_low), .en(Load_ALU_HI), .Q(ALU_Out), .clk(CLK));  // open: clr
  Register #(.width(32)) u_HI_Out (.D(ZF_high), .en(Load_ALU_HI), .Q(HI_Out), .clk(CLK));  // open: clr

  // Other names for the same wires on the sheet: A_out[6:0] = out_33; TTY[6:0] = out_33; Func_Code[5:0] = out_32;
  //   I0[31:0] = in_1; I1[31:0] = in_4; I2[31:0] = in_2; I3[31:0] = in_5; Load_A_B = Load_A_and_B; O0[31:0] = out_25;
  //   O1[31:0] = out_27; O2[31:0] = out_26; O3[31:0] = out_28; Op_Code[5:0] = out_31; PC_EN = jump

  // Notes on the sheet:
  //   REVISAR
endmodule

module Instruction_Data_Memory (
  input  [31:0] in_1,
  input  [31:0] in_2,
  input  [31:0] in_3,
  input  [31:0] in_4,
  input  [31:0] Address,
  input  [31:0] in_6,
  output [31:0] out_7,
  output [31:0] out_8,
  output [31:0] out_9,
  output [31:0] out_10,
  output [31:0] out_11,
  output [15:0] Address_2,
  output [3:0] MASK
);

  wire not_1_out, not_2_out, not_3_out, not_4_out;

  and and_1 (MASK[3], Address[2], Address[3]);
  not not_1 (not_1_out, Address[2]);
  not not_2 (not_2_out, Address[3]);
  not not_3 (not_3_out, Address[2]);
  not not_4 (not_4_out, Address[3]);
  and and_2 (MASK[2], not_1_out, Address[3]);
  and and_3 (MASK[1], not_2_out, Address[2]);
  and and_4 (MASK[0], not_3_out, not_4_out);
  Multiplexer #(.select(2), .width(32), .enable("false")) multiplexer_1 (
    .in0(in_1), .in1(in_3), .in2(in_2), .in3(in_4),
    .out({out_7[7:0], out_7[15:8], out_7[23:16], out_7[31:24]}), .sel(Address[3:2]));

  assign Address_2 = Address[19:4];
  assign out_8 = {in_6[7:0], in_6[15:8], in_6[23:16], in_6[31:24]};
  assign out_9 = {in_6[7:0], in_6[15:8], in_6[23:16], in_6[31:24]};
  assign out_10 = {in_6[7:0], in_6[15:8], in_6[23:16], in_6[31:24]};
  assign out_11 = {in_6[7:0], in_6[15:8], in_6[23:16], in_6[31:24]};

  // Other names for the same wires on the sheet: Bank_SEL[1:0] = Address[3:2]; Address_to_RAM[15:0] = Address[19:4];
  //   I0[31:0] = in_1; I1[31:0] = in_3; I2[31:0] = in_2; I3[31:0] = in_4; RD[31:0] = out_7;
  //   WD[31:0] = {in_6[7:0], in_6[15:8], in_6[23:16], in_6[31:24]}
endmodule
