// Logisim project Instruction Decoder.circ as structural Verilog: 1 circuit, main circuit Instruction Decoder
module Instruction_Decoder (
  input  [31:0] Instruction,
  output [25:0] out_2,
  output [4:0] out_3,
  output [4:0] out_4,
  output [4:0] out_5,
  output [15:0] out_6,
  output [5:0] out_7,
  output [5:0] out_8
);

  wire add, add_ALU, addi, \and , and_ALU, andi, beq, bgtz, blez, bltz, bne, div, divu, halt, j, jr, kbd, lw,
       Math_op_out, mfhi, mflo, mult, mulu, nop, \nor , \or , or_ALU, ori, pop_push_out, rnd, slt, slt_ALU,
       slti, sltiu, sltu, sltu_ALU, Special_out, sub, sw, tty, \xor , xor_ALU, xori;
  wire [3:0] ALU_OP_Code;

  and Math_op (Math_op_out, ~Instruction[26], ~Instruction[27], ~Instruction[28], ~Instruction[29], ~Instruction[30], ~Instruction[31]);  // AND_Gate
  and pop_push (pop_push_out, ~Instruction[26], ~Instruction[27], ~Instruction[28], Instruction[29], Instruction[30], Instruction[31]);  // AND_Gate
  and Special (Special_out, Instruction[26], Instruction[27], Instruction[28], Instruction[29], Instruction[30], Instruction[31]);
  and u_add (add, ~Instruction[0], ~Instruction[1], ~Instruction[2], ~Instruction[3], ~Instruction[4], Instruction[5]);  // AND_Gate
  and u_div (div, ~Instruction[0], Instruction[1], ~Instruction[2], Instruction[3], Instruction[4], ~Instruction[5]);  // AND_Gate
  and u_nor (\nor , Instruction[0], Instruction[1], Instruction[2], ~Instruction[3], ~Instruction[4], Instruction[5]);  // AND_Gate
  and u_mfhi (mfhi, ~Instruction[0], ~Instruction[1], ~Instruction[2], ~Instruction[3], Instruction[4], ~Instruction[5]);  // AND_Gate
  and u_halt (halt, Instruction[0], Instruction[1], Instruction[2], Instruction[3], Instruction[4], Instruction[5]);
  and u_Sub (sub, ~Instruction[0], Instruction[1], ~Instruction[2], ~Instruction[3], ~Instruction[4], Instruction[5]);  // AND_Gate
  and u_divu (divu, Instruction[0], Instruction[1], ~Instruction[2], Instruction[3], Instruction[4], ~Instruction[5]);  // AND_Gate
  and u_xor (\xor , ~Instruction[0], ~Instruction[1], ~Instruction[2], Instruction[3], ~Instruction[4], Instruction[5]);  // AND_Gate
  and u_mflo (mflo, ~Instruction[0], Instruction[1], ~Instruction[2], ~Instruction[3], Instruction[4], ~Instruction[5]);  // AND_Gate
  and u_tty (tty, Instruction[0], ~Instruction[1], ~Instruction[2], ~Instruction[3], ~Instruction[4], ~Instruction[5]);  // AND_Gate
  and u_addi (addi, ~Instruction[26], ~Instruction[27], ~Instruction[28], Instruction[29], ~Instruction[30], ~Instruction[31]);  // AND_Gate
  and u_andi (andi, ~Instruction[26], ~Instruction[27], Instruction[28], Instruction[29], ~Instruction[30], ~Instruction[31]);  // AND_Gate
  and u_slti (slti, ~Instruction[26], Instruction[27], ~Instruction[28], Instruction[29], ~Instruction[30], ~Instruction[31]);  // AND_Gate
  and u_beq (beq, ~Instruction[26], ~Instruction[27], Instruction[28], ~Instruction[29], ~Instruction[30], ~Instruction[31]);  // AND_Gate
  and u_bne (bne, Instruction[26], ~Instruction[27], Instruction[28], ~Instruction[29], ~Instruction[30], ~Instruction[31]);  // AND_Gate
  and u_mult (mult, ~Instruction[0], ~Instruction[1], ~Instruction[2], Instruction[3], Instruction[4], ~Instruction[5]);  // AND_Gate
  and u_and (\and , ~Instruction[0], ~Instruction[1], Instruction[2], ~Instruction[3], ~Instruction[4], Instruction[5]);  // AND_Gate
  and u_slt (slt, ~Instruction[0], Instruction[1], ~Instruction[2], Instruction[3], ~Instruction[4], Instruction[5]);  // AND_Gate
  and u_nop (nop, ~Instruction[0], ~Instruction[1], ~Instruction[2], ~Instruction[3], ~Instruction[4], ~Instruction[5]);  // AND_Gate
  and u_rnd (rnd, ~Instruction[0], Instruction[1], ~Instruction[2], ~Instruction[3], ~Instruction[4], ~Instruction[5]);  // AND_Gate
  and u_blez (blez, ~Instruction[26], Instruction[27], Instruction[28], ~Instruction[29], ~Instruction[30], ~Instruction[31]);  // AND_Gate
  and u_bgtz (bgtz, Instruction[26], Instruction[27], Instruction[28], ~Instruction[29], ~Instruction[30], ~Instruction[31]);  // AND_Gate
  and u_bltz (bltz, Instruction[26], ~Instruction[27], ~Instruction[28], ~Instruction[29], ~Instruction[30], ~Instruction[31]);  // AND_Gate
  and u_lw (lw, Instruction[26], Instruction[27], ~Instruction[28], ~Instruction[29], ~Instruction[30], Instruction[31]);  // AND_Gate
  and u_sw (sw, Instruction[26], Instruction[27], ~Instruction[28], Instruction[29], ~Instruction[30], Instruction[31]);  // AND_Gate
  and u_sltiu (sltiu, Instruction[26], Instruction[27], ~Instruction[28], Instruction[29], ~Instruction[30], ~Instruction[31]);  // AND_Gate
  and u_ori (ori, Instruction[26], ~Instruction[27], Instruction[28], Instruction[29], ~Instruction[30], ~Instruction[31]);  // AND_Gate
  and u_xori (xori, ~Instruction[26], Instruction[27], Instruction[28], Instruction[29], ~Instruction[30], ~Instruction[31]);  // AND_Gate
  and u_mulu (mulu, Instruction[0], ~Instruction[1], ~Instruction[2], Instruction[3], Instruction[4], ~Instruction[5]);  // AND_Gate
  and u_or (\or , Instruction[0], ~Instruction[1], Instruction[2], ~Instruction[3], ~Instruction[4], Instruction[5]);  // AND_Gate
  and u_sltu (sltu, Instruction[0], Instruction[1], ~Instruction[2], Instruction[3], ~Instruction[4], Instruction[5]);  // AND_Gate
  and u_jr (jr, ~Instruction[0], ~Instruction[1], ~Instruction[2], Instruction[3], ~Instruction[4], ~Instruction[5]);  // AND_Gate
  and u_kbd (kbd, ~Instruction[0], ~Instruction[1], Instruction[2], ~Instruction[3], ~Instruction[4], ~Instruction[5]);  // AND_Gate
  or or_2 (and_ALU, \and , andi);
  or or_3 (add_ALU, add, addi);
  or or_4 (or_ALU, \or , ori);
  Priority_Encoder #(.select(4)) priority_encoder_1 (
    .in0(mult), .in1(mulu), .in2(div), .in3(divu), .in4(and_ALU), .in5(sub), .in6(xor_ALU), .in7(add_ALU),
    .in8(or_ALU), .in9(sltu_ALU), .in10(\nor ), .in11(slt_ALU), .out(ALU_OP_Code));  // open: in12, in13, in14, in15, gs, en_out, en_in
  or or_5 (slt_ALU, slt, slti);
  or or_6 (sltu_ALU, sltu, sltiu);
  or or_7 (xor_ALU, \xor , xori);
  and u_j (j, ~Instruction[26], Instruction[27], ~Instruction[28], ~Instruction[29], ~Instruction[30], ~Instruction[31]);  // AND_Gate

  assign out_2 = Instruction[25:0];
  assign out_3 = Instruction[25:21];
  assign out_4 = Instruction[20:16];
  assign out_5 = Instruction[15:11];
  assign out_6 = Instruction[15:0];
  assign out_7 = Instruction[31:26];
  assign out_8 = Instruction[5:0];

  // Other names for the same wires on the sheet: Constante[15:0] = Instruction[15:0];
  //   Destino_Salto[25:0] = Instruction[25:0]; Func_code[5:0] = Instruction[5:0]; x[4:0] = Instruction[10:6];
  //   Rd[4:0] = Instruction[15:11]; Rt[4:0] = Instruction[20:16]; Rs[4:0] = Instruction[25:21];
  //   Op_Code[5:0] = Instruction[31:26]

  // Notes on the sheet:
  //   Op-Code
  //   Tipo R
  //   Func-Code
  //   Instruction Decoder
  //   Tipo I
  //   Tipo J
  //   Outpout
endmodule
