// Logisim project Register File CPU.circ as structural Verilog: 1 circuit, main circuit main
module main (
  input  [4:0] \Dirección_de_destino ,
  input  R_W,
  input  [31:0] Datos_de_entrada,
  input  [4:0] Selector_Salida_A,
  input  [4:0] Selector_Salida_B,
  input  Reset,
  input  Clock,
  input  [31:0] HI_in,
  input  [31:0] LO_in,
  input  R_W_HI_LO,
  output [31:0] Salida_A,
  output [31:0] Salida_B,
  output [31:0] out_13,
  output [31:0] out_14
);

  wire L01, L02, L03, L04, L05, L06, L07, L08, L09, L10, L11, L12, L13, L14, L15, L16, L17, L18, L19, L20,
       L21, L22, L23, L24, L25, L26, L27, L28, L29, L30, L31;
  wire [31:0] Q00, Q01, Q02, Q03, Q04, Q05, Q06, Q07, Q08, Q09, Q10, Q11, Q12, Q13, Q14, Q15, Q16, Q17, Q18,
       Q19, Q20, Q21, Q22, Q23, Q24, Q25, Q26, Q27, Q28, Q29, Q30, Q31;

  Register #(.width(32)) HI (.D(HI_in), .en(R_W_HI_LO), .Q(out_13), .clk(Clock), .clr(Reset));
  Demultiplexer #(.select(5), .enable("false")) demultiplexer_1 (
    .out1(L01), .out2(L02), .out3(L03), .out4(L04), .out5(L05), .out6(L06), .out7(L07), .out8(L08),
    .out9(L09), .out10(L10), .out11(L11), .out12(L12), .out13(L13), .out14(L14), .out15(L15), .out16(L16),
    .out17(L17), .out18(L18), .out19(L19), .out20(L20), .out21(L21), .out22(L22), .out23(L23), .out24(L24),
    .out25(L25), .out26(L26), .out27(L27), .out28(L28), .out29(L29), .out30(L30), .out31(L31), .in(R_W),
    .sel(\Dirección_de_destino ));  // open: out0
  Register #(.width(32)) LO (.D(LO_in), .en(R_W_HI_LO), .Q(out_14), .clk(Clock), .clr(Reset));
  Register #(.width(32)) R00 (.Q(Q00));  // open: D, en, clk, clr
  Register #(.width(32)) R04 (.D(Datos_de_entrada), .en(L04), .Q(Q04), .clk(Clock), .clr(Reset));
  Register #(.width(32)) R08 (.D(Datos_de_entrada), .en(L08), .Q(Q08), .clk(Clock), .clr(Reset));
  Register #(.width(32)) R12 (.D(Datos_de_entrada), .en(L12), .Q(Q12), .clk(Clock), .clr(Reset));
  Register #(.width(32)) R16 (.D(Datos_de_entrada), .en(L16), .Q(Q16), .clk(Clock), .clr(Reset));
  Register #(.width(32)) R20 (.D(Datos_de_entrada), .en(L20), .Q(Q20), .clk(Clock), .clr(Reset));
  Register #(.width(32)) R24 (.D(Datos_de_entrada), .en(L24), .Q(Q24), .clk(Clock), .clr(Reset));
  Register #(.width(32)) R28 (.D(Datos_de_entrada), .en(L28), .Q(Q28), .clk(Clock), .clr(Reset));
  Register #(.width(32)) R01 (.D(Datos_de_entrada), .en(L01), .Q(Q01), .clk(Clock), .clr(Reset));
  Register #(.width(32)) R05 (.D(Datos_de_entrada), .en(L05), .Q(Q05), .clk(Clock), .clr(Reset));
  Register #(.width(32)) R09 (.D(Datos_de_entrada), .en(L09), .Q(Q09), .clk(Clock), .clr(Reset));
  Register #(.width(32)) R13 (.D(Datos_de_entrada), .en(L13), .Q(Q13), .clk(Clock), .clr(Reset));
  Register #(.width(32)) R17 (.D(Datos_de_entrada), .en(L17), .Q(Q17), .clk(Clock), .clr(Reset));
  Register #(.width(32)) R21 (.D(Datos_de_entrada), .en(L21), .Q(Q21), .clk(Clock), .clr(Reset));
  Register #(.width(32)) R25 (.D(Datos_de_entrada), .en(L25), .Q(Q25), .clk(Clock), .clr(Reset));
  Register #(.width(32)) R29 (.D(Datos_de_entrada), .en(L29), .Q(Q29), .clk(Clock), .clr(Reset));
  Register #(.width(32)) R02 (.D(Datos_de_entrada), .en(L02), .Q(Q02), .clk(Clock), .clr(Reset));
  Register #(.width(32)) R06 (.D(Datos_de_entrada), .en(L06), .Q(Q06), .clk(Clock), .clr(Reset));
  Register #(.width(32)) R10 (.D(Datos_de_entrada), .en(L10), .Q(Q10), .clk(Clock), .clr(Reset));
  Register #(.width(32)) R14 (.D(Datos_de_entrada), .en(L14), .Q(Q14), .clk(Clock), .clr(Reset));
  Register #(.width(32)) R18 (.D(Datos_de_entrada), .en(L18), .Q(Q18), .clk(Clock), .clr(Reset));
  Register #(.width(32)) R22 (.D(Datos_de_entrada), .en(L22), .Q(Q22), .clk(Clock), .clr(Reset));
  Register #(.width(32)) R26 (.D(Datos_de_entrada), .en(L26), .Q(Q26), .clk(Clock), .clr(Reset));
  Register #(.width(32)) R30 (.D(Datos_de_entrada), .en(L30), .Q(Q30), .clk(Clock), .clr(Reset));
  Register #(.width(32)) R03 (.D(Datos_de_entrada), .en(L03), .Q(Q03), .clk(Clock), .clr(Reset));
  Register #(.width(32)) R07 (.D(Datos_de_entrada), .en(L07), .Q(Q07), .clk(Clock), .clr(Reset));
  Register #(.width(32)) R11 (.D(Datos_de_entrada), .en(L11), .Q(Q11), .clk(Clock), .clr(Reset));
  Register #(.width(32)) R15 (.D(Datos_de_entrada), .en(L15), .Q(Q15), .clk(Clock), .clr(Reset));
  Register #(.width(32)) R19 (.D(Datos_de_entrada), .en(L19), .Q(Q19), .clk(Clock), .clr(Reset));
  Register #(.width(32)) R23 (.D(Datos_de_entrada), .en(L23), .Q(Q23), .clk(Clock), .clr(Reset));
  Register #(.width(32)) R27 (.D(Datos_de_entrada), .en(L27), .Q(Q27), .clk(Clock), .clr(Reset));
  Register #(.width(32)) R31 (.D(Datos_de_entrada), .en(L31), .Q(Q31), .clk(Clock), .clr(Reset));
  Multiplexer #(.select(5), .width(32), .enable("false")) multiplexer_1 (
    .in0(Q00), .in1(Q01), .in2(Q02), .in3(Q03), .in4(Q04), .in5(Q05), .in6(Q06), .in7(Q07), .in8(Q08),
    .in9(Q09), .in10(Q10), .in11(Q11), .in12(Q12), .in13(Q13), .in14(Q14), .in15(Q15), .in16(Q16),
    .in17(Q17), .in18(Q18), .in19(Q19), .in20(Q20), .in21(Q21), .in22(Q22), .in23(Q23), .in24(Q24),
    .in25(Q25), .in26(Q26), .in27(Q27), .in28(Q28), .in29(Q29), .in30(Q30), .in31(Q31), .out(Salida_A),
    .sel(Selector_Salida_A));
  Multiplexer #(.select(5), .width(32), .enable("false")) multiplexer_2 (
    .in0(Q00), .in1(Q01), .in2(Q02), .in3(Q03), .in4(Q04), .in5(Q05), .in6(Q06), .in7(Q07), .in8(Q08),
    .in9(Q09), .in10(Q10), .in11(Q11), .in12(Q12), .in13(Q13), .in14(Q14), .in15(Q15), .in16(Q16),
    .in17(Q17), .in18(Q18), .in19(Q19), .in20(Q20), .in21(Q21), .in22(Q22), .in23(Q23), .in24(Q24),
    .in25(Q25), .in26(Q26), .in27(Q27), .in28(Q28), .in29(Q29), .in30(Q30), .in31(Q31), .out(Salida_B),
    .sel(Selector_Salida_B));

  // Other names for the same wires on the sheet: CLK = Clock; DI[31:0] = Datos_de_entrada;
  //   DirS[4:0] = \Dirección_de_destino ; R = Reset; SA[4:0] = Selector_Salida_A; SB[4:0] = Selector_Salida_B

  // Notes on the sheet:
  //   Registros HI y LO
  //   Register File de 32 Registros y 32 bits
endmodule
