// Logisim project alu.circ as structural Verilog: 3 circuits, main circuit ALU
module ALU (
  input  [31:0] Input_0,
  input  [31:0] Input_1,
  input  [3:0] OpCode,
  output [31:0] Result_Low,
  output [31:0] High,
  output ZF,
  output NF
);

  wire Borrow_Out, Carry, comparator_1_lt, comparator_2_lt, EN;
  wire [31:0] add, \and , div_High, div_Low, divu_High, divu_Low, mult_High, mult_Low, mulu_High, mulu_Low,
       \nor , \or , SCmp, sub, UCmp, \xor ;

  Comparator #(.width(32)) comparator_1 (.a(Input_0), .b(Input_1), .lt(comparator_1_lt));  // open: gt, eq
  assign SCmp = {{31{1'b0}}, comparator_1_lt};  // Bit_Extender bit_extender_1
  Adder #(.width(32)) adder_1 (.a(Input_0), .b(Input_1), .out(add), .cout(Carry));  // open: cin
  Subtractor #(.width(32)) subtractor_1 (.a(Input_0), .b(Input_1), .out(sub), .bout(Borrow_Out));  // open: bin
  Multiplier #(.width(32)) multiplier_1 (.a(Input_0), .b(Input_1), .out(mulu_Low), .cout(mulu_High));  // open: cin
  Divider #(.width(32)) divider_1 (.a(Input_0), .b(Input_1), .out(divu_Low), .rem(divu_High));  // open: upper
  Comparator #(.width(32), .mode("unsigned")) comparator_2 (
    .a(Input_0), .b(Input_1), .lt(comparator_2_lt));  // open: gt, eq
  SMul smul_1 (.I0(Input_0), .I1(Input_1), .Low(mult_Low), .High(mult_High));
  SDiv sdiv_1 (.I0(Input_0), .I1(Input_1), .Low(div_Low), .High(div_High));
  assign UCmp = {{31{1'b0}}, comparator_2_lt};  // Bit_Extender bit_extender_2
  assign \and  = Input_0 & Input_1;  // AND_Gate and_1, 32 bits wide
  assign \or  = Input_0 | Input_1;  // OR_Gate or_1, 32 bits wide
  assign \xor  = Input_0 ^ Input_1;  // XOR_Gate xor_1, 32 bits wide
  assign \nor  = ~(Input_0 | Input_1);  // NOR_Gate nor_1, 32 bits wide
  nor nor_2 (EN, OpCode[3], OpCode[2]);
  Multiplexer #(.select(4), .width(32), .enable("false")) multiplexer_1 (
    .in0(mult_Low), .in1(mulu_Low), .in2(div_Low), .in3(divu_Low), .in4(\and ), .in5(sub), .in6(\xor ),
    .in7(add), .in8(\or ), .in9(UCmp), .in10(\nor ), .in11(SCmp), .in12(Input_1), .in13(Input_0),
    .out(Result_Low), .sel(OpCode));  // open: in14, in15
  Multiplexer #(.select(2), .width(32)) multiplexer_2 (
    .in0(mult_High), .in1(mulu_High), .in2(div_High), .in3(divu_High), .out(High), .sel(OpCode[1:0]), .en(EN));
  Comparator #(.width(32)) comparator_3 (.a(Result_Low), .b({32{1'b0}}), .eq(ZF), .lt(NF));  // open: gt

  // Other names for the same wires on the sheet: High_Sel[1:0] = OpCode[1:0]

  // Notes on the sheet:
  //   Inputs
  //   Signed comparer
  //   add
  //   sub
  //   mulu
  //   divu
  //   Arithmetic Operations
  //   Unsigned comparer
  //   mult
  //   div
  //   and
  //   or
  //   xor
  //   nor
  //   Logical Operations
  //   Outputs
endmodule

module SMul (
  input  [31:0] I0,
  input  [31:0] I1,
  output [31:0] Low,
  output [31:0] High
);

  wire adder_1_cout, XOR;
  wire [31:0] adder_1_out, adder_2_out, bit_extender_1_out, multiplexer_1_out, multiplexer_2_out,
       multiplier_1_cout, multiplier_1_out, negator_1_out, negator_2_out, not_1_out, not_2_out;

  xor xor_1 (XOR, I0[31], I1[31]);
  Multiplexer #(.width(32), .enable("false")) multiplexer_1 (
    .in0(I0), .in1(negator_1_out), .out(multiplexer_1_out), .sel(I0[31]));
  Negator #(.width(32)) negator_1 (.in(I0), .out(negator_1_out));
  Multiplexer #(.width(32), .enable("false")) multiplexer_2 (
    .in0(I1), .in1(negator_2_out), .out(multiplexer_2_out), .sel(I1[31]));
  Negator #(.width(32)) negator_2 (.in(I1), .out(negator_2_out));
  Multiplier #(.width(32)) multiplier_1 (
    .a(multiplexer_1_out), .b(multiplexer_2_out), .out(multiplier_1_out), .cout(multiplier_1_cout));  // open: cin
  assign not_1_out = ~multiplier_1_out;  // NOT_Gate not_1, 32 bits wide
  Adder #(.width(32)) adder_1 (.a(not_1_out), .b(32'h1), .out(adder_1_out), .cout(adder_1_cout));  // open: cin
  assign not_2_out = ~multiplier_1_cout;  // NOT_Gate not_2, 32 bits wide
  Adder #(.width(32)) adder_2 (.a(not_2_out), .b(bit_extender_1_out), .out(adder_2_out));  // open: cin, cout
  assign bit_extender_1_out = {{31{1'b0}}, adder_1_cout};  // Bit_Extender bit_extender_1
  Multiplexer #(.width(32), .enable("false")) multiplexer_3 (
    .in0(multiplier_1_out), .in1(adder_1_out), .out(Low), .sel(XOR));
  Multiplexer #(.width(32), .enable("false")) multiplexer_4 (
    .in0(multiplier_1_cout), .in1(adder_2_out), .out(High), .sel(XOR));

  // Other names for the same wires on the sheet: MSB_I0 = I0[31]; MSB_I1 = I1[31]
endmodule

module SDiv (
  input  [31:0] I0,
  input  [31:0] I1,
  output [31:0] Low,
  output [31:0] High
);

  wire adder_1_cout, XOR;
  wire [31:0] adder_1_out, adder_2_out, bit_extender_1_out, divider_1_out, divider_1_rem, multiplexer_1_out,
       multiplexer_2_out, negator_1_out, negator_2_out, not_1_out, not_2_out;

  xor xor_1 (XOR, I0[31], I1[31]);
  Multiplexer #(.width(32)) multiplexer_1 (
    .in0(I0), .in1(negator_1_out), .out(multiplexer_1_out), .sel(I0[31]));  // open: en
  Negator #(.width(32)) negator_1 (.in(I0), .out(negator_1_out));
  Multiplexer #(.width(32)) multiplexer_2 (
    .in0(I1), .in1(negator_2_out), .out(multiplexer_2_out), .sel(I1[31]));  // open: en
  Negator #(.width(32)) negator_2 (.in(I1), .out(negator_2_out));
  Divider #(.width(32)) divider_1 (
    .a(multiplexer_1_out), .b(multiplexer_2_out), .out(divider_1_out), .rem(divider_1_rem));  // open: upper
  assign not_1_out = ~divider_1_out;  // NOT_Gate not_1, 32 bits wide
  Adder #(.width(32)) adder_1 (.a(not_1_out), .b(32'h1), .out(adder_1_out), .cout(adder_1_cout));  // open: cin
  assign not_2_out = ~divider_1_rem;  // NOT_Gate not_2, 32 bits wide
  Adder #(.width(32)) adder_2 (.a(not_2_out), .b(bit_extender_1_out), .out(adder_2_out));  // open: cin, cout
  assign bit_extender_1_out = {{31{1'b0}}, adder_1_cout};  // Bit_Extender bit_extender_1
  Multiplexer #(.width(32)) multiplexer_3 (.in0(divider_1_out), .in1(adder_1_out), .out(Low), .sel(XOR));  // open: en
  Multiplexer #(.width(32)) multiplexer_4 (.in0(divider_1_rem), .in1(adder_2_out), .out(High), .sel(XOR));  // open: en

  // Other names for the same wires on the sheet: MSB_I0 = I0[31]; MSB_I1 = I1[31]
endmodule
